// Digital circuit QT Sandbox.dig as structural Verilog
module QT_Sandbox (
  input  clk,
  input  [7:0] Input
);

  wire interface_q1_1_reading, interface_q1_1_writing, qtc_1_p6, qtc_1_p8, qtc_1_p9, Read_out, Send_out,
       Turn_On_out;
  wire [7:0] interface_q1_1_comp_out, interface_q1_1_user_out, qtc_1_p7;

  Button Turn_On (.out(Turn_On_out));
  Button Send (.out(Send_out));
  Button Read (.out(Read_out));
  Interface_Q1 interface_q1_1 (
    .Clk_In(clk), .Send(Send_out), .Read(Read_out), .User_In(Input), .Comp_In(qtc_1_p7), .RP(qtc_1_p8),
    .WP(qtc_1_p9), .User_Out(interface_q1_1_user_out), .Writing(interface_q1_1_writing),
    .Comp_Out(interface_q1_1_comp_out), .Reading(interface_q1_1_reading));
  // Probe Output on interface_q1_1_user_out
  // QTC qtc_1: pin names not known; wires that end beside it: Turn_On_out, clk, interface_q1_1_writing, interface_q1_1_comp_out, interface_q1_1_reading, qtc_1_p6, qtc_1_p7, qtc_1_p8, qtc_1_p9
  LED led_1 (.in(qtc_1_p6));

  // Notes on the sheet:
  //   clk: Hz: 32
endmodule
